// Logisim project 32b_single_cycle_cpu_single_page1.circ as structural Verilog: 1 circuit, main circuit main
module main (
);

  wire and_1_out, and_4_out, and_10_out, and_11_out, and_12_out, and_14_out, and_15_out, and_16_out,
       and_17_out, and_18_out, and_19_out, and_20_out, and_21_out, and_22_out, and_23_out, and_24_out,
       and_25_out, and_26_out, and_27_out, and_28_out, and_29_out, and_30_out, and_31_out, and_32_out,
       and_33_out, and_34_out, and_35_out, and_36_out, and_37_out, and_38_out, and_39_out, and_40_out,
       and_41_out, and_42_out, and_43_out, and_60_out, and_61_out, and_62_out, and_63_out, and_64_out,
       and_65_out, and_66_out, and_67_out, and_68_out, and_69_out, and_70_out, and_71_out, and_72_out,
       and_73_out, and_74_out, and_75_out, and_76_out, and_77_out, and_78_out, and_79_out, and_80_out,
       and_81_out, and_82_out, and_83_out, and_84_out, and_85_out, and_86_out, and_87_out, and_88_out,
       and_89_out, and_90_out, and_91_out, and_108_out, and_109_out, and_110_out, and_111_out, and_112_out,
       and_113_out, and_114_out, and_115_out, and_116_out, and_117_out, and_118_out, and_119_out,
       and_120_out, and_121_out, and_122_out, and_123_out, and_124_out, and_125_out, and_126_out,
       and_127_out, and_128_out, and_129_out, and_130_out, and_131_out, and_132_out, and_133_out,
       and_134_out, and_135_out, and_136_out, and_137_out, and_138_out, and_139_out, and_156_out,
       and_157_out, and_158_out, and_159_out, and_160_out, and_161_out, and_162_out, and_163_out,
       and_164_out, and_165_out, and_166_out, and_167_out, and_168_out, and_169_out, and_170_out,
       and_171_out, and_172_out, and_173_out, and_174_out, and_175_out, and_176_out, and_177_out,
       and_178_out, and_179_out, and_180_out, and_181_out, and_182_out, and_183_out, and_184_out,
       and_185_out, and_186_out, and_187_out, clock_1_out, comparator_1_eq, comparator_2_gt, comparator_3_eq,
       comparator_3_lt, comparator_4_eq, comparator_4_lt, comparator_5_lt, comparator_6_lt, decoder_1_out0,
       decoder_1_out1, decoder_1_out2, decoder_1_out3, decoder_1_out4, decoder_1_out5, decoder_1_out6,
       decoder_1_out7, decoder_2_out4, decoder_2_out5, decoder_2_out8, decoder_2_out12, decoder_2_out13,
       decoder_2_out24, decoder_2_out25, decoder_2_out27, multiplexer_2_out, multiplexer_3_out, nor_1_out,
       not_1_out, or_1_out, or_3_out, or_4_out, or_6_out, or_7_out, or_8_out, xor_1_out, xor_2_out;
  wire [1:0] decoder_2_out0;
  wire [15:0] adder_2_out, and_13_out, and_44_out, and_45_out, and_46_out, and_47_out, and_48_out,
       and_49_out, and_50_out, and_51_out, and_52_out, and_53_out, and_54_out, and_55_out, and_56_out,
       and_57_out, and_58_out, and_59_out, and_92_out, and_93_out, and_94_out, and_95_out, and_96_out,
       and_97_out, and_98_out, and_99_out, and_100_out, and_101_out, and_102_out, and_103_out, and_104_out,
       and_105_out, and_106_out, and_107_out, and_140_out, and_141_out, and_142_out, and_143_out,
       and_144_out, and_145_out, and_146_out, and_147_out, and_148_out, and_149_out, and_150_out,
       and_151_out, and_152_out, and_153_out, and_154_out, and_155_out, and_188_out, and_189_out,
       and_190_out, and_191_out, and_192_out, and_193_out, and_194_out, and_195_out, and_196_out,
       and_197_out, and_198_out, and_199_out, and_200_out, and_201_out, and_202_out, and_203_out,
       bit_extender_12_out, bit_extender_13_out, bit_extender_14_out, bit_extender_15_out,
       bit_extender_16_out, bit_extender_17_out, bit_extender_18_out, bit_extender_19_out,
       bit_extender_20_out, bit_extender_21_out, bit_extender_22_out, bit_extender_23_out,
       bit_extender_24_out, bit_extender_25_out, bit_extender_26_out, bit_extender_27_out,
       bit_extender_28_out, bit_extender_29_out, bit_extender_30_out, bit_extender_31_out,
       bit_extender_32_out, bit_extender_33_out, bit_extender_34_out, bit_extender_35_out,
       bit_extender_36_out, bit_extender_37_out, bit_extender_38_out, bit_extender_39_out,
       bit_extender_40_out, bit_extender_41_out, bit_extender_42_out, bit_extender_43_out,
       bit_extender_44_out, bit_extender_45_out, bit_extender_46_out, bit_extender_47_out,
       bit_extender_48_out, bit_extender_49_out, bit_extender_50_out, bit_extender_51_out,
       bit_extender_52_out, bit_extender_53_out, bit_extender_54_out, bit_extender_55_out,
       bit_extender_56_out, bit_extender_57_out, bit_extender_58_out, bit_extender_59_out,
       bit_extender_60_out, bit_extender_61_out, bit_extender_62_out, bit_extender_63_out,
       bit_extender_64_out, bit_extender_65_out, bit_extender_66_out, bit_extender_67_out,
       bit_extender_68_out, bit_extender_69_out, bit_extender_70_out, bit_extender_71_out,
       bit_extender_72_out, bit_extender_73_out, bit_extender_74_out, bit_extender_75_out,
       bit_extender_76_out, bit_extender_77_out, DMEM_dout, multiplexer_4_out, multiplexer_5_out,
       multiplexer_6_out, multiplexer_8_out, multiplexer_9_out, multiplexer_11_out, or_5_out, or_12_out,
       or_13_out, or_14_out, or_15_out, or_16_out, or_17_out, or_18_out, or_19_out, or_20_out, or_21_out,
       or_22_out, or_23_out, or_24_out, or_25_out, or_26_out, or_27_out, or_28_out, or_29_out, or_30_out,
       or_31_out, or_32_out, or_33_out, or_34_out, or_35_out, or_36_out, or_37_out, or_38_out, or_39_out,
       or_40_out, or_41_out, or_42_out, or_43_out, or_44_out, or_45_out, or_46_out, or_47_out, or_48_out,
       or_49_out, or_50_out, or_51_out, or_52_out, or_53_out, or_54_out, or_55_out, or_56_out, or_57_out,
       or_58_out, or_59_out, or_60_out, or_61_out, or_62_out, or_63_out, or_64_out, or_65_out, or_66_out,
       or_67_out, or_68_out, or_69_out, or_70_out, or_71_out, register_1_q, register_1_q_2, register_2_q,
       register_2_q_2, register_3_q, register_3_q_2, register_4_q, register_4_q_2, register_5_q,
       register_5_q_2, register_9_q, register_10_q, register_11_q, register_12_q, register_13_q,
       register_14_q, register_15_q, register_16_q, register_17_q, register_18_q, register_19_q,
       register_20_q, register_21_q, register_22_q, register_23_q, register_24_q, register_25_q,
       register_26_q, register_27_q, register_28_q, register_29_q, register_30_q, register_31_q,
       register_32_q, register_33_q, register_34_q, register_35_q, register_36_q, register_37_q,
       register_38_q, register_39_q, shifter_1_out, subtractor_1_out, xor_3_out;
  wire [16:0] multiplexer_7_out, shifter_2_out, shifter_3_out;
  wire [23:0] and_2_out, and_3_out, bit_extender_1_out, bit_extender_2_out;
  wire [31:0] adder_1_out, and_5_out, and_6_out, and_7_out, and_8_out, and_9_out, bit_extender_3_out,
       bit_extender_4_out, bit_extender_5_out, bit_extender_6_out, bit_extender_7_out, bit_extender_8_out,
       bit_extender_9_out, bit_extender_10_out, bit_extender_11_out, IMEM_dout, multiplexer_1_out,
       multiplexer_10_out, or_2_out, or_10_out, or_11_out, PC_q, register_6_q, register_7_q, register_8_q;

  Clock clock_1 (.out(clock_1_out));
  RAM #(.addrWidth(24), .dataWidth(32), .trigger("high"), .databus("bibus")) IMEM (
    .addr(PC_q[23:0]), .we(1'b0), .oe(1'b1), .dout(IMEM_dout));  // open: din
  RAM #(.addrWidth(24), .dataWidth(16), .trigger("falling"), .databus("bibus")) DMEM (
    .addr(and_2_out), .we(and_1_out), .oe(1'b1), .clk(clock_1_out), .din(or_11_out[15:0]), .dout(DMEM_dout));
  Comparator #(.width(6), .mode("unsigned")) comparator_1 (
    .a(multiplexer_10_out[31:26]), .b({6{1'b0}}), .eq(comparator_1_eq));  // open: gt, lt
  and and_1 (and_1_out, decoder_2_out8, comparator_1_eq);
  assign bit_extender_1_out = {{23{comparator_1_eq}}, comparator_1_eq};  // Bit_Extender bit_extender_1
  assign and_2_out = bit_extender_1_out & multiplexer_10_out[25:2];  // AND_Gate and_2, 24 bits wide
  Comparator #(.width(6), .mode("unsigned")) comparator_2 (
    .a(multiplexer_10_out[31:26]), .b({6{1'b0}}), .gt(comparator_2_gt));  // open: eq, lt
  Comparator #(.width(32)) comparator_3 (
    .a(or_10_out), .b(or_11_out), .eq(comparator_3_eq), .lt(comparator_3_lt));  // open: gt
  Comparator #(.width(32), .mode("unsigned")) comparator_4 (
    .a(or_10_out), .b(or_11_out), .eq(comparator_4_eq), .lt(comparator_4_lt));  // open: gt
  assign bit_extender_2_out = {{23{comparator_2_gt}}, comparator_2_gt};  // Bit_Extender bit_extender_2
  Adder #(.width(32)) adder_1 (.a(PC_q), .b(32'h4), .out(adder_1_out));  // open: cin, cout
  Register #(.width(32)) PC (.D(multiplexer_1_out), .en(1'b1), .clk(clock_1_out), .Q(PC_q));  // open: clr
  Multiplexer #(.width(32), .enable("false")) multiplexer_1 (
    .in0(adder_1_out), .in1(multiplexer_10_out), .out(multiplexer_1_out), .sel(or_7_out));
  Multiplexer #(.enable("false")) multiplexer_2 (
    .in0(comparator_3_eq), .in1(comparator_4_eq), .out(multiplexer_2_out), .sel(IMEM_dout[13]));
  Multiplexer #(.enable("false")) multiplexer_3 (
    .in0(comparator_3_lt), .in1(comparator_4_lt), .out(multiplexer_3_out), .sel(IMEM_dout[13]));
  assign and_3_out = multiplexer_10_out[25:2] & bit_extender_2_out;  // AND_Gate and_3, 24 bits wide
  Decoder #(.select(3)) decoder_1 (
    .out0(decoder_1_out0), .out1(decoder_1_out1), .out2(decoder_1_out2), .out3(decoder_1_out3),
    .out4(decoder_1_out4), .out5(decoder_1_out5), .out6(decoder_1_out6), .out7(decoder_1_out7),
    .sel(and_3_out[2:0]), .en(and_4_out));
  and and_4 (and_4_out, comparator_2_gt, decoder_2_out8);
  TTY tty_1 (.data(or_11_out[6:0]), .clk(clock_1_out));  // open: we, clr
  assign bit_extender_3_out = {{31{or_1_out}}, or_1_out};  // Bit_Extender bit_extender_3
  assign and_5_out = bit_extender_3_out & bit_extender_4_out;  // AND_Gate and_5, 32 bits wide
  assign bit_extender_4_out = {{20{IMEM_dout[31]}}, IMEM_dout[31:20]};  // Bit_Extender bit_extender_4
  assign bit_extender_5_out = {{31{decoder_2_out8}}, decoder_2_out8};  // Bit_Extender bit_extender_5
  assign and_6_out = bit_extender_5_out & bit_extender_6_out;  // AND_Gate and_6, 32 bits wide
  assign bit_extender_6_out = {{20{IMEM_dout[31]}}, {IMEM_dout[31:25], IMEM_dout[11:7]}};  // Bit_Extender bit_extender_6
  assign bit_extender_7_out = {{31{decoder_2_out24}}, decoder_2_out24};  // Bit_Extender bit_extender_7
  assign and_7_out = bit_extender_7_out & bit_extender_8_out;  // AND_Gate and_7, 32 bits wide
  assign bit_extender_8_out = {{19{IMEM_dout[31]}}, {IMEM_dout[31], IMEM_dout[7], IMEM_dout[30:25], IMEM_dout[11:8], 1'b0}};  // Bit_Extender bit_extender_8
  assign bit_extender_9_out = {{31{or_4_out}}, or_4_out};  // Bit_Extender bit_extender_9
  assign and_8_out = bit_extender_9_out & {IMEM_dout[31:12], {12{1'b0}}};  // AND_Gate and_8, 32 bits wide
  assign bit_extender_10_out = {{31{decoder_2_out27}}, decoder_2_out27};  // Bit_Extender bit_extender_10
  assign and_9_out = bit_extender_10_out & bit_extender_11_out;  // AND_Gate and_9, 32 bits wide
  assign bit_extender_11_out = {{11{IMEM_dout[31]}}, {IMEM_dout[31], IMEM_dout[19:12], IMEM_dout[20], IMEM_dout[30:21], 1'b0}};  // Bit_Extender bit_extender_11
  xor xor_1 (xor_1_out, IMEM_dout[12], multiplexer_2_out);
  xor xor_2 (xor_2_out, IMEM_dout[12], multiplexer_3_out);
  Register #(.width(32)) register_1 (
    .D(or_11_out), .en(decoder_1_out0), .clk(clock_1_out), .Q({register_1_q_2, register_1_q}));  // open: clr
  Register #(.width(32)) register_2 (
    .D(or_11_out), .en(decoder_1_out4), .clk(clock_1_out), .Q({register_2_q_2, register_2_q}));  // open: clr
  Decoder #(.select(5), .enable("false")) decoder_2 (
    .out0(decoder_2_out0[0]), .out4(decoder_2_out4), .out5(decoder_2_out5), .out8(decoder_2_out8),
    .out12(decoder_2_out12), .out13(decoder_2_out13), .out24(decoder_2_out24), .out25(decoder_2_out25),
    .out27(decoder_2_out27), .sel(IMEM_dout[6:2]));  // open: out1, out2, out3, out6, out7, out9, out10, out11, out14, out15, out16, out17, out18, out19, out20, out21, out22, out23, out26, out28, out29, out30, out31
  or or_1 (or_1_out, decoder_2_out0[0], decoder_2_out4, decoder_2_out25);
  assign or_2_out = and_5_out | and_6_out | and_7_out | and_8_out | and_9_out;  // OR_Gate or_2, 32 bits wide
  and and_10 (and_10_out, ~IMEM_dout[14], xor_1_out);  // AND_Gate
  or or_3 (or_3_out, and_10_out, and_11_out);
  and and_11 (and_11_out, IMEM_dout[14], xor_2_out);
  or or_4 (or_4_out, decoder_2_out5, decoder_2_out13);
  Register #(.width(32)) register_3 (
    .D(or_11_out), .en(decoder_1_out1), .clk(clock_1_out), .Q({register_3_q_2, register_3_q}));  // open: clr
  Register #(.width(32)) register_4 (
    .D(or_11_out), .en(decoder_1_out5), .clk(clock_1_out), .Q({register_4_q_2, register_4_q}));  // open: clr
  and and_12 (and_12_out, decoder_2_out24, or_3_out);
  Multiplexer #(.width(16), .enable("false")) multiplexer_4 (
    .in0(or_10_out[15:0]), .in1(PC_q[15:0]), .out(multiplexer_4_out), .sel(or_6_out));
  Multiplexer #(.width(16), .enable("false")) multiplexer_5 (
    .in0(or_11_out[15:0]), .in1(or_2_out[15:0]), .out(multiplexer_5_out), .sel(not_1_out));
  Adder #(.width(16)) adder_2 (.a(multiplexer_4_out), .b(multiplexer_5_out), .out(adder_2_out));  // open: cin, cout
  Subtractor #(.width(16)) subtractor_1 (
    .a(multiplexer_4_out), .b(multiplexer_5_out), .out(subtractor_1_out));  // open: bin, bout
  Shifter #(.width(16)) shifter_1 (.in(multiplexer_4_out), .\dist (multiplexer_5_out[3:0]), .out(shifter_1_out));
  Comparator #(.width(16)) comparator_5 (
    .a(multiplexer_4_out), .b(multiplexer_5_out), .lt(comparator_5_lt));  // open: gt, eq
  Comparator #(.width(16), .mode("unsigned")) comparator_6 (
    .a(multiplexer_4_out), .b(multiplexer_5_out), .lt(comparator_6_lt));  // open: gt, eq
  assign xor_3_out = multiplexer_4_out ^ multiplexer_5_out;  // XOR_Gate xor_3, 16 bits wide
  Shifter #(.width(16), .shift("lr")) shifter_2 (
    .in(multiplexer_4_out), .\dist (multiplexer_5_out[3:0]), .out(shifter_2_out[15:0]));
  Shifter #(.width(16), .shift("ar")) shifter_3 (
    .in(multiplexer_4_out), .\dist (multiplexer_5_out[3:0]), .out(shifter_3_out[15:0]));
  assign or_5_out = multiplexer_4_out | multiplexer_5_out;  // OR_Gate or_5, 16 bits wide
  assign and_13_out = multiplexer_4_out & multiplexer_5_out;  // AND_Gate and_13, 16 bits wide
  Register #(.width(32)) register_5 (
    .D(or_11_out), .en(decoder_1_out2), .clk(clock_1_out), .Q({register_5_q_2, register_5_q}));  // open: clr
  Register #(.width(32)) register_6 (
    .D(or_11_out), .en(decoder_1_out6), .clk(clock_1_out), .Q(register_6_q));  // open: clr
  or or_6 (or_6_out, decoder_2_out27, decoder_2_out24);
  not not_1 (not_1_out, decoder_2_out12);
  or or_7 (or_7_out, and_12_out, decoder_2_out25, decoder_2_out27);
  Multiplexer #(.width(16), .enable("false")) multiplexer_6 (
    .in0(adder_2_out), .in1(subtractor_1_out), .out(multiplexer_6_out), .sel(IMEM_dout[30]));
  assign bit_extender_12_out = {{15{1'b0}}, comparator_5_lt};  // Bit_Extender bit_extender_12
  assign bit_extender_13_out = {{15{1'b0}}, comparator_6_lt};  // Bit_Extender bit_extender_13
  Multiplexer #(.width(17), .enable("false")) multiplexer_7 (
    .in0(shifter_2_out), .in1(shifter_3_out), .out(multiplexer_7_out), .sel(IMEM_dout[30]));
  or or_8 (or_8_out, decoder_2_out4, decoder_2_out12);
  or or_9 (decoder_2_out0[1], decoder_2_out25, decoder_2_out27);
  Multiplexer #(.select(3), .width(16), .enable("false")) multiplexer_8 (
    .in0(multiplexer_6_out), .in1(shifter_1_out), .in2(bit_extender_12_out), .in3(bit_extender_13_out),
    .in4(xor_3_out), .in5(multiplexer_7_out[15:0]), .in6(or_5_out), .in7(and_13_out),
    .out(multiplexer_8_out), .sel(IMEM_dout[14:12]));
  Register #(.width(32)) register_7 (
    .D(or_11_out), .en(decoder_1_out3), .clk(clock_1_out), .Q(register_7_q));  // open: clr
  Register #(.width(32)) register_8 (
    .D(or_11_out), .en(decoder_1_out7), .clk(clock_1_out), .Q(register_8_q));  // open: clr
  nor nor_1 (nor_1_out, decoder_2_out8, decoder_2_out24);
  Multiplexer #(.width(16), .enable("false")) multiplexer_9 (
    .in0(adder_2_out), .in1(multiplexer_8_out), .out(multiplexer_9_out), .sel(or_8_out));
  Multiplexer #(.width(16), .enable("false")) multiplexer_10 (
    .in0(multiplexer_9_out), .in1(multiplexer_5_out), .out(multiplexer_10_out[15:0]), .sel(decoder_2_out13));
  Multiplexer #(.select(2), .width(16), .enable("false")) multiplexer_11 (
    .in0(multiplexer_10_out[15:0]), .in1(DMEM_dout), .in2(adder_1_out[15:0]), .out(multiplexer_11_out),
    .sel(decoder_2_out0));  // open: in3
  and and_14 (and_14_out, ~IMEM_dout[15], ~IMEM_dout[16], ~IMEM_dout[17], ~IMEM_dout[18], ~IMEM_dout[19]);  // AND_Gate
  and and_15 (and_15_out, ~IMEM_dout[20], ~IMEM_dout[21], ~IMEM_dout[22], ~IMEM_dout[23], ~IMEM_dout[24]);  // AND_Gate
  and and_16 (and_16_out, nor_1_out, and_17_out);
  and and_17 (and_17_out, IMEM_dout[7], ~IMEM_dout[8], ~IMEM_dout[9], ~IMEM_dout[10], ~IMEM_dout[11]);  // AND_Gate
  and and_18 (and_18_out, IMEM_dout[15], ~IMEM_dout[16], ~IMEM_dout[17], ~IMEM_dout[18], ~IMEM_dout[19]);  // AND_Gate
  and and_19 (and_19_out, IMEM_dout[20], ~IMEM_dout[21], ~IMEM_dout[22], ~IMEM_dout[23], ~IMEM_dout[24]);  // AND_Gate
  and and_20 (and_20_out, nor_1_out, and_21_out);
  and and_21 (and_21_out, ~IMEM_dout[7], IMEM_dout[8], ~IMEM_dout[9], ~IMEM_dout[10], ~IMEM_dout[11]);  // AND_Gate
  and and_22 (and_22_out, ~IMEM_dout[15], IMEM_dout[16], ~IMEM_dout[17], ~IMEM_dout[18], ~IMEM_dout[19]);  // AND_Gate
  and and_23 (and_23_out, ~IMEM_dout[20], IMEM_dout[21], ~IMEM_dout[22], ~IMEM_dout[23], ~IMEM_dout[24]);  // AND_Gate
  and and_24 (and_24_out, nor_1_out, and_25_out);
  and and_25 (and_25_out, IMEM_dout[7], IMEM_dout[8], ~IMEM_dout[9], ~IMEM_dout[10], ~IMEM_dout[11]);  // AND_Gate
  and and_26 (and_26_out, IMEM_dout[15], IMEM_dout[16], ~IMEM_dout[17], ~IMEM_dout[18], ~IMEM_dout[19]);  // AND_Gate
  and and_27 (and_27_out, IMEM_dout[20], IMEM_dout[21], ~IMEM_dout[22], ~IMEM_dout[23], ~IMEM_dout[24]);  // AND_Gate
  and and_28 (and_28_out, nor_1_out, and_29_out);
  and and_29 (and_29_out, ~IMEM_dout[7], ~IMEM_dout[8], IMEM_dout[9], ~IMEM_dout[10], ~IMEM_dout[11]);  // AND_Gate
  and and_30 (and_30_out, ~IMEM_dout[15], ~IMEM_dout[16], IMEM_dout[17], ~IMEM_dout[18], ~IMEM_dout[19]);  // AND_Gate
  and and_31 (and_31_out, ~IMEM_dout[20], ~IMEM_dout[21], IMEM_dout[22], ~IMEM_dout[23], ~IMEM_dout[24]);  // AND_Gate
  and and_32 (and_32_out, nor_1_out, and_33_out);
  and and_33 (and_33_out, IMEM_dout[7], ~IMEM_dout[8], IMEM_dout[9], ~IMEM_dout[10], ~IMEM_dout[11]);  // AND_Gate
  and and_34 (and_34_out, IMEM_dout[15], ~IMEM_dout[16], IMEM_dout[17], ~IMEM_dout[18], ~IMEM_dout[19]);  // AND_Gate
  and and_35 (and_35_out, IMEM_dout[20], ~IMEM_dout[21], IMEM_dout[22], ~IMEM_dout[23], ~IMEM_dout[24]);  // AND_Gate
  and and_36 (and_36_out, nor_1_out, and_37_out);
  and and_37 (and_37_out, ~IMEM_dout[7], IMEM_dout[8], IMEM_dout[9], ~IMEM_dout[10], ~IMEM_dout[11]);  // AND_Gate
  and and_38 (and_38_out, ~IMEM_dout[15], IMEM_dout[16], IMEM_dout[17], ~IMEM_dout[18], ~IMEM_dout[19]);  // AND_Gate
  and and_39 (and_39_out, ~IMEM_dout[20], IMEM_dout[21], IMEM_dout[22], ~IMEM_dout[23], ~IMEM_dout[24]);  // AND_Gate
  and and_40 (and_40_out, nor_1_out, and_41_out);
  and and_41 (and_41_out, IMEM_dout[7], IMEM_dout[8], IMEM_dout[9], ~IMEM_dout[10], ~IMEM_dout[11]);  // AND_Gate
  and and_42 (and_42_out, IMEM_dout[15], IMEM_dout[16], IMEM_dout[17], ~IMEM_dout[18], ~IMEM_dout[19]);  // AND_Gate
  and and_43 (and_43_out, IMEM_dout[20], IMEM_dout[21], IMEM_dout[22], ~IMEM_dout[23], ~IMEM_dout[24]);  // AND_Gate
  Register #(.width(16)) register_9 (
    .D(multiplexer_11_out), .en(and_16_out), .clk(clock_1_out), .Q(register_9_q));  // open: clr
  Register #(.width(16)) register_10 (
    .D(multiplexer_11_out), .en(and_20_out), .clk(clock_1_out), .Q(register_10_q));  // open: clr
  Register #(.width(16)) register_11 (
    .D(multiplexer_11_out), .en(and_24_out), .clk(clock_1_out), .Q(register_11_q));  // open: clr
  Register #(.width(16)) register_12 (
    .D(multiplexer_11_out), .en(and_28_out), .clk(clock_1_out), .Q(register_12_q));  // open: clr
  Register #(.width(16)) register_13 (
    .D(multiplexer_11_out), .en(and_32_out), .clk(clock_1_out), .Q(register_13_q));  // open: clr
  Register #(.width(16)) register_14 (
    .D(multiplexer_11_out), .en(and_36_out), .clk(clock_1_out), .Q(register_14_q));  // open: clr
  Register #(.width(16)) register_15 (
    .D(multiplexer_11_out), .en(and_40_out), .clk(clock_1_out), .Q(register_15_q));  // open: clr
  assign or_10_out[15:0] = or_26_out | or_12_out;  // OR_Gate or_10, 16 bits wide
  assign or_11_out[15:0] = or_27_out | or_13_out;  // OR_Gate or_11, 16 bits wide
  assign and_44_out = {16{1'b0}} & bit_extender_14_out;  // AND_Gate and_44, 16 bits wide
  assign and_45_out = {16{1'b0}} & bit_extender_15_out;  // AND_Gate and_45, 16 bits wide
  assign bit_extender_14_out = {{15{and_14_out}}, and_14_out};  // Bit_Extender bit_extender_14
  assign bit_extender_15_out = {{15{and_15_out}}, and_15_out};  // Bit_Extender bit_extender_15
  assign and_46_out = register_9_q & bit_extender_16_out;  // AND_Gate and_46, 16 bits wide
  assign and_47_out = register_9_q & bit_extender_17_out;  // AND_Gate and_47, 16 bits wide
  assign bit_extender_16_out = {{15{and_18_out}}, and_18_out};  // Bit_Extender bit_extender_16
  assign bit_extender_17_out = {{15{and_19_out}}, and_19_out};  // Bit_Extender bit_extender_17
  assign and_48_out = register_10_q & bit_extender_18_out;  // AND_Gate and_48, 16 bits wide
  assign and_49_out = register_10_q & bit_extender_19_out;  // AND_Gate and_49, 16 bits wide
  assign bit_extender_18_out = {{15{and_22_out}}, and_22_out};  // Bit_Extender bit_extender_18
  assign bit_extender_19_out = {{15{and_23_out}}, and_23_out};  // Bit_Extender bit_extender_19
  assign and_50_out = register_11_q & bit_extender_20_out;  // AND_Gate and_50, 16 bits wide
  assign and_51_out = register_11_q & bit_extender_21_out;  // AND_Gate and_51, 16 bits wide
  assign bit_extender_20_out = {{15{and_26_out}}, and_26_out};  // Bit_Extender bit_extender_20
  assign bit_extender_21_out = {{15{and_27_out}}, and_27_out};  // Bit_Extender bit_extender_21
  assign and_52_out = register_12_q & bit_extender_22_out;  // AND_Gate and_52, 16 bits wide
  assign and_53_out = register_12_q & bit_extender_23_out;  // AND_Gate and_53, 16 bits wide
  assign bit_extender_22_out = {{15{and_30_out}}, and_30_out};  // Bit_Extender bit_extender_22
  assign bit_extender_23_out = {{15{and_31_out}}, and_31_out};  // Bit_Extender bit_extender_23
  assign and_54_out = register_13_q & bit_extender_24_out;  // AND_Gate and_54, 16 bits wide
  assign and_55_out = register_13_q & bit_extender_25_out;  // AND_Gate and_55, 16 bits wide
  assign bit_extender_24_out = {{15{and_34_out}}, and_34_out};  // Bit_Extender bit_extender_24
  assign bit_extender_25_out = {{15{and_35_out}}, and_35_out};  // Bit_Extender bit_extender_25
  assign and_56_out = register_14_q & bit_extender_26_out;  // AND_Gate and_56, 16 bits wide
  assign and_57_out = register_14_q & bit_extender_27_out;  // AND_Gate and_57, 16 bits wide
  assign bit_extender_26_out = {{15{and_38_out}}, and_38_out};  // Bit_Extender bit_extender_26
  assign bit_extender_27_out = {{15{and_39_out}}, and_39_out};  // Bit_Extender bit_extender_27
  assign and_58_out = register_15_q & bit_extender_28_out;  // AND_Gate and_58, 16 bits wide
  assign and_59_out = register_15_q & bit_extender_29_out;  // AND_Gate and_59, 16 bits wide
  assign bit_extender_28_out = {{15{and_42_out}}, and_42_out};  // Bit_Extender bit_extender_28
  assign bit_extender_29_out = {{15{and_43_out}}, and_43_out};  // Bit_Extender bit_extender_29
  assign or_12_out = and_44_out | or_14_out;  // OR_Gate or_12, 16 bits wide
  assign or_13_out = and_45_out | or_15_out;  // OR_Gate or_13, 16 bits wide
  assign or_14_out = and_46_out | or_16_out;  // OR_Gate or_14, 16 bits wide
  assign or_15_out = and_47_out | or_17_out;  // OR_Gate or_15, 16 bits wide
  assign or_16_out = and_48_out | or_18_out;  // OR_Gate or_16, 16 bits wide
  assign or_17_out = and_49_out | or_19_out;  // OR_Gate or_17, 16 bits wide
  assign or_18_out = and_50_out | or_20_out;  // OR_Gate or_18, 16 bits wide
  assign or_19_out = and_51_out | or_21_out;  // OR_Gate or_19, 16 bits wide
  assign or_20_out = and_52_out | or_22_out;  // OR_Gate or_20, 16 bits wide
  assign or_21_out = and_53_out | or_23_out;  // OR_Gate or_21, 16 bits wide
  assign or_22_out = and_54_out | or_24_out;  // OR_Gate or_22, 16 bits wide
  assign or_23_out = and_55_out | or_25_out;  // OR_Gate or_23, 16 bits wide
  assign or_24_out = and_56_out | and_58_out;  // OR_Gate or_24, 16 bits wide
  assign or_25_out = and_57_out | and_59_out;  // OR_Gate or_25, 16 bits wide
  and and_60 (and_60_out, ~IMEM_dout[7], ~IMEM_dout[8], ~IMEM_dout[9], IMEM_dout[10], ~IMEM_dout[11]);  // AND_Gate
  and and_61 (and_61_out, ~IMEM_dout[15], ~IMEM_dout[16], ~IMEM_dout[17], IMEM_dout[18], ~IMEM_dout[19]);  // AND_Gate
  and and_62 (and_62_out, ~IMEM_dout[20], ~IMEM_dout[21], ~IMEM_dout[22], IMEM_dout[23], ~IMEM_dout[24]);  // AND_Gate
  and and_63 (and_63_out, IMEM_dout[7], ~IMEM_dout[8], ~IMEM_dout[9], IMEM_dout[10], ~IMEM_dout[11]);  // AND_Gate
  and and_64 (and_64_out, IMEM_dout[15], ~IMEM_dout[16], ~IMEM_dout[17], IMEM_dout[18], ~IMEM_dout[19]);  // AND_Gate
  and and_65 (and_65_out, IMEM_dout[20], ~IMEM_dout[21], ~IMEM_dout[22], IMEM_dout[23], ~IMEM_dout[24]);  // AND_Gate
  and and_66 (and_66_out, ~IMEM_dout[7], IMEM_dout[8], ~IMEM_dout[9], IMEM_dout[10], ~IMEM_dout[11]);  // AND_Gate
  and and_67 (and_67_out, ~IMEM_dout[15], IMEM_dout[16], ~IMEM_dout[17], IMEM_dout[18], ~IMEM_dout[19]);  // AND_Gate
  and and_68 (and_68_out, ~IMEM_dout[20], IMEM_dout[21], ~IMEM_dout[22], IMEM_dout[23], ~IMEM_dout[24]);  // AND_Gate
  and and_69 (and_69_out, IMEM_dout[7], IMEM_dout[8], ~IMEM_dout[9], IMEM_dout[10], ~IMEM_dout[11]);  // AND_Gate
  and and_70 (and_70_out, IMEM_dout[15], IMEM_dout[16], ~IMEM_dout[17], IMEM_dout[18], ~IMEM_dout[19]);  // AND_Gate
  and and_71 (and_71_out, IMEM_dout[20], IMEM_dout[21], ~IMEM_dout[22], IMEM_dout[23], ~IMEM_dout[24]);  // AND_Gate
  and and_72 (and_72_out, ~IMEM_dout[7], ~IMEM_dout[8], IMEM_dout[9], IMEM_dout[10], ~IMEM_dout[11]);  // AND_Gate
  and and_73 (and_73_out, ~IMEM_dout[15], ~IMEM_dout[16], IMEM_dout[17], IMEM_dout[18], ~IMEM_dout[19]);  // AND_Gate
  and and_74 (and_74_out, ~IMEM_dout[20], ~IMEM_dout[21], IMEM_dout[22], IMEM_dout[23], ~IMEM_dout[24]);  // AND_Gate
  and and_75 (and_75_out, IMEM_dout[7], ~IMEM_dout[8], IMEM_dout[9], IMEM_dout[10], ~IMEM_dout[11]);  // AND_Gate
  and and_76 (and_76_out, IMEM_dout[15], ~IMEM_dout[16], IMEM_dout[17], IMEM_dout[18], ~IMEM_dout[19]);  // AND_Gate
  and and_77 (and_77_out, IMEM_dout[20], ~IMEM_dout[21], IMEM_dout[22], IMEM_dout[23], ~IMEM_dout[24]);  // AND_Gate
  and and_78 (and_78_out, ~IMEM_dout[7], IMEM_dout[8], IMEM_dout[9], IMEM_dout[10], ~IMEM_dout[11]);  // AND_Gate
  and and_79 (and_79_out, ~IMEM_dout[15], IMEM_dout[16], IMEM_dout[17], IMEM_dout[18], ~IMEM_dout[19]);  // AND_Gate
  and and_80 (and_80_out, ~IMEM_dout[20], IMEM_dout[21], IMEM_dout[22], IMEM_dout[23], ~IMEM_dout[24]);  // AND_Gate
  and and_81 (and_81_out, IMEM_dout[7], IMEM_dout[8], IMEM_dout[9], IMEM_dout[10], ~IMEM_dout[11]);  // AND_Gate
  and and_82 (and_82_out, IMEM_dout[15], IMEM_dout[16], IMEM_dout[17], IMEM_dout[18], ~IMEM_dout[19]);  // AND_Gate
  and and_83 (and_83_out, IMEM_dout[20], IMEM_dout[21], IMEM_dout[22], IMEM_dout[23], ~IMEM_dout[24]);  // AND_Gate
  Register #(.width(16)) register_16 (
    .D(multiplexer_11_out), .en(and_84_out), .clk(clock_1_out), .Q(register_16_q));  // open: clr
  and and_84 (and_84_out, nor_1_out, and_60_out);
  Register #(.width(16)) register_17 (
    .D(multiplexer_11_out), .en(and_85_out), .clk(clock_1_out), .Q(register_17_q));  // open: clr
  and and_85 (and_85_out, nor_1_out, and_63_out);
  Register #(.width(16)) register_18 (
    .D(multiplexer_11_out), .en(and_86_out), .clk(clock_1_out), .Q(register_18_q));  // open: clr
  and and_86 (and_86_out, nor_1_out, and_66_out);
  Register #(.width(16)) register_19 (
    .D(multiplexer_11_out), .en(and_87_out), .clk(clock_1_out), .Q(register_19_q));  // open: clr
  and and_87 (and_87_out, nor_1_out, and_69_out);
  Register #(.width(16)) register_20 (
    .D(multiplexer_11_out), .en(and_88_out), .clk(clock_1_out), .Q(register_20_q));  // open: clr
  and and_88 (and_88_out, nor_1_out, and_72_out);
  Register #(.width(16)) register_21 (
    .D(multiplexer_11_out), .en(and_89_out), .clk(clock_1_out), .Q(register_21_q));  // open: clr
  and and_89 (and_89_out, nor_1_out, and_75_out);
  Register #(.width(16)) register_22 (
    .D(multiplexer_11_out), .en(and_90_out), .clk(clock_1_out), .Q(register_22_q));  // open: clr
  and and_90 (and_90_out, nor_1_out, and_78_out);
  Register #(.width(16)) register_23 (
    .D(multiplexer_11_out), .en(and_91_out), .clk(clock_1_out), .Q(register_23_q));  // open: clr
  and and_91 (and_91_out, nor_1_out, and_81_out);
  assign or_26_out = or_42_out | or_28_out;  // OR_Gate or_26, 16 bits wide
  assign bit_extender_30_out = {{15{and_61_out}}, and_61_out};  // Bit_Extender bit_extender_30
  assign bit_extender_31_out = {{15{and_62_out}}, and_62_out};  // Bit_Extender bit_extender_31
  assign bit_extender_32_out = {{15{and_64_out}}, and_64_out};  // Bit_Extender bit_extender_32
  assign bit_extender_33_out = {{15{and_65_out}}, and_65_out};  // Bit_Extender bit_extender_33
  assign bit_extender_34_out = {{15{and_67_out}}, and_67_out};  // Bit_Extender bit_extender_34
  assign bit_extender_35_out = {{15{and_68_out}}, and_68_out};  // Bit_Extender bit_extender_35
  assign bit_extender_36_out = {{15{and_70_out}}, and_70_out};  // Bit_Extender bit_extender_36
  assign bit_extender_37_out = {{15{and_71_out}}, and_71_out};  // Bit_Extender bit_extender_37
  assign bit_extender_38_out = {{15{and_73_out}}, and_73_out};  // Bit_Extender bit_extender_38
  assign bit_extender_39_out = {{15{and_74_out}}, and_74_out};  // Bit_Extender bit_extender_39
  assign bit_extender_40_out = {{15{and_76_out}}, and_76_out};  // Bit_Extender bit_extender_40
  assign bit_extender_41_out = {{15{and_77_out}}, and_77_out};  // Bit_Extender bit_extender_41
  assign bit_extender_42_out = {{15{and_79_out}}, and_79_out};  // Bit_Extender bit_extender_42
  assign bit_extender_43_out = {{15{and_80_out}}, and_80_out};  // Bit_Extender bit_extender_43
  assign bit_extender_44_out = {{15{and_82_out}}, and_82_out};  // Bit_Extender bit_extender_44
  assign bit_extender_45_out = {{15{and_83_out}}, and_83_out};  // Bit_Extender bit_extender_45
  assign or_27_out = or_43_out | or_29_out;  // OR_Gate or_27, 16 bits wide
  assign or_28_out = and_92_out | or_30_out;  // OR_Gate or_28, 16 bits wide
  assign or_29_out = and_93_out | or_31_out;  // OR_Gate or_29, 16 bits wide
  assign and_92_out = register_16_q & bit_extender_30_out;  // AND_Gate and_92, 16 bits wide
  assign and_93_out = register_16_q & bit_extender_31_out;  // AND_Gate and_93, 16 bits wide
  assign or_30_out = and_94_out | or_32_out;  // OR_Gate or_30, 16 bits wide
  assign or_31_out = and_95_out | or_33_out;  // OR_Gate or_31, 16 bits wide
  assign and_94_out = register_17_q & bit_extender_32_out;  // AND_Gate and_94, 16 bits wide
  assign and_95_out = register_17_q & bit_extender_33_out;  // AND_Gate and_95, 16 bits wide
  assign or_32_out = and_96_out | or_34_out;  // OR_Gate or_32, 16 bits wide
  assign or_33_out = and_97_out | or_35_out;  // OR_Gate or_33, 16 bits wide
  assign and_96_out = register_18_q & bit_extender_34_out;  // AND_Gate and_96, 16 bits wide
  assign and_97_out = register_18_q & bit_extender_35_out;  // AND_Gate and_97, 16 bits wide
  assign or_34_out = and_98_out | or_36_out;  // OR_Gate or_34, 16 bits wide
  assign or_35_out = and_99_out | or_37_out;  // OR_Gate or_35, 16 bits wide
  assign and_98_out = register_19_q & bit_extender_36_out;  // AND_Gate and_98, 16 bits wide
  assign and_99_out = register_19_q & bit_extender_37_out;  // AND_Gate and_99, 16 bits wide
  assign or_36_out = and_100_out | or_38_out;  // OR_Gate or_36, 16 bits wide
  assign or_37_out = and_101_out | or_39_out;  // OR_Gate or_37, 16 bits wide
  assign and_100_out = register_20_q & bit_extender_38_out;  // AND_Gate and_100, 16 bits wide
  assign and_101_out = register_20_q & bit_extender_39_out;  // AND_Gate and_101, 16 bits wide
  assign or_38_out = and_102_out | or_40_out;  // OR_Gate or_38, 16 bits wide
  assign or_39_out = and_103_out | or_41_out;  // OR_Gate or_39, 16 bits wide
  assign and_102_out = register_21_q & bit_extender_40_out;  // AND_Gate and_102, 16 bits wide
  assign and_103_out = register_21_q & bit_extender_41_out;  // AND_Gate and_103, 16 bits wide
  assign or_40_out = and_104_out | and_106_out;  // OR_Gate or_40, 16 bits wide
  assign or_41_out = and_105_out | and_107_out;  // OR_Gate or_41, 16 bits wide
  assign and_104_out = register_22_q & bit_extender_42_out;  // AND_Gate and_104, 16 bits wide
  assign and_105_out = register_22_q & bit_extender_43_out;  // AND_Gate and_105, 16 bits wide
  assign and_106_out = register_23_q & bit_extender_44_out;  // AND_Gate and_106, 16 bits wide
  assign and_107_out = register_23_q & bit_extender_45_out;  // AND_Gate and_107, 16 bits wide
  and and_108 (and_108_out, nor_1_out, and_109_out);
  and and_109 (and_109_out, ~IMEM_dout[7], ~IMEM_dout[8], ~IMEM_dout[9], ~IMEM_dout[10], IMEM_dout[11]);  // AND_Gate
  and and_110 (and_110_out, ~IMEM_dout[15], ~IMEM_dout[16], ~IMEM_dout[17], ~IMEM_dout[18], IMEM_dout[19]);  // AND_Gate
  and and_111 (and_111_out, ~IMEM_dout[20], ~IMEM_dout[21], ~IMEM_dout[22], ~IMEM_dout[23], IMEM_dout[24]);  // AND_Gate
  and and_112 (and_112_out, nor_1_out, and_113_out);
  and and_113 (and_113_out, IMEM_dout[7], ~IMEM_dout[8], ~IMEM_dout[9], ~IMEM_dout[10], IMEM_dout[11]);  // AND_Gate
  and and_114 (and_114_out, IMEM_dout[15], ~IMEM_dout[16], ~IMEM_dout[17], ~IMEM_dout[18], IMEM_dout[19]);  // AND_Gate
  and and_115 (and_115_out, IMEM_dout[20], ~IMEM_dout[21], ~IMEM_dout[22], ~IMEM_dout[23], IMEM_dout[24]);  // AND_Gate
  and and_116 (and_116_out, nor_1_out, and_117_out);
  and and_117 (and_117_out, ~IMEM_dout[7], IMEM_dout[8], ~IMEM_dout[9], ~IMEM_dout[10], IMEM_dout[11]);  // AND_Gate
  and and_118 (and_118_out, ~IMEM_dout[15], IMEM_dout[16], ~IMEM_dout[17], ~IMEM_dout[18], IMEM_dout[19]);  // AND_Gate
  and and_119 (and_119_out, ~IMEM_dout[20], IMEM_dout[21], ~IMEM_dout[22], ~IMEM_dout[23], IMEM_dout[24]);  // AND_Gate
  and and_120 (and_120_out, nor_1_out, and_121_out);
  and and_121 (and_121_out, IMEM_dout[7], IMEM_dout[8], ~IMEM_dout[9], ~IMEM_dout[10], IMEM_dout[11]);  // AND_Gate
  and and_122 (and_122_out, IMEM_dout[15], IMEM_dout[16], ~IMEM_dout[17], ~IMEM_dout[18], IMEM_dout[19]);  // AND_Gate
  and and_123 (and_123_out, IMEM_dout[20], IMEM_dout[21], ~IMEM_dout[22], ~IMEM_dout[23], IMEM_dout[24]);  // AND_Gate
  and and_124 (and_124_out, nor_1_out, and_125_out);
  and and_125 (and_125_out, ~IMEM_dout[7], ~IMEM_dout[8], IMEM_dout[9], ~IMEM_dout[10], IMEM_dout[11]);  // AND_Gate
  and and_126 (and_126_out, ~IMEM_dout[15], ~IMEM_dout[16], IMEM_dout[17], ~IMEM_dout[18], IMEM_dout[19]);  // AND_Gate
  and and_127 (and_127_out, ~IMEM_dout[20], ~IMEM_dout[21], IMEM_dout[22], ~IMEM_dout[23], IMEM_dout[24]);  // AND_Gate
  and and_128 (and_128_out, nor_1_out, and_129_out);
  and and_129 (and_129_out, IMEM_dout[7], ~IMEM_dout[8], IMEM_dout[9], ~IMEM_dout[10], IMEM_dout[11]);  // AND_Gate
  and and_130 (and_130_out, IMEM_dout[15], ~IMEM_dout[16], IMEM_dout[17], ~IMEM_dout[18], IMEM_dout[19]);  // AND_Gate
  and and_131 (and_131_out, IMEM_dout[20], ~IMEM_dout[21], IMEM_dout[22], ~IMEM_dout[23], IMEM_dout[24]);  // AND_Gate
  and and_132 (and_132_out, nor_1_out, and_133_out);
  and and_133 (and_133_out, ~IMEM_dout[7], IMEM_dout[8], IMEM_dout[9], ~IMEM_dout[10], IMEM_dout[11]);  // AND_Gate
  and and_134 (and_134_out, ~IMEM_dout[15], IMEM_dout[16], IMEM_dout[17], ~IMEM_dout[18], IMEM_dout[19]);  // AND_Gate
  and and_135 (and_135_out, ~IMEM_dout[20], IMEM_dout[21], IMEM_dout[22], ~IMEM_dout[23], IMEM_dout[24]);  // AND_Gate
  and and_136 (and_136_out, nor_1_out, and_137_out);
  and and_137 (and_137_out, IMEM_dout[7], IMEM_dout[8], IMEM_dout[9], ~IMEM_dout[10], IMEM_dout[11]);  // AND_Gate
  and and_138 (and_138_out, IMEM_dout[15], IMEM_dout[16], IMEM_dout[17], ~IMEM_dout[18], IMEM_dout[19]);  // AND_Gate
  and and_139 (and_139_out, IMEM_dout[20], IMEM_dout[21], IMEM_dout[22], ~IMEM_dout[23], IMEM_dout[24]);  // AND_Gate
  assign or_42_out = or_58_out | or_44_out;  // OR_Gate or_42, 16 bits wide
  Register #(.width(16)) register_24 (
    .D(multiplexer_11_out), .en(and_108_out), .clk(clock_1_out), .Q(register_24_q));  // open: clr
  assign bit_extender_46_out = {{15{and_110_out}}, and_110_out};  // Bit_Extender bit_extender_46
  assign bit_extender_47_out = {{15{and_111_out}}, and_111_out};  // Bit_Extender bit_extender_47
  Register #(.width(16)) register_25 (
    .D(multiplexer_11_out), .en(and_112_out), .clk(clock_1_out), .Q(register_25_q));  // open: clr
  assign bit_extender_48_out = {{15{and_114_out}}, and_114_out};  // Bit_Extender bit_extender_48
  assign bit_extender_49_out = {{15{and_115_out}}, and_115_out};  // Bit_Extender bit_extender_49
  Register #(.width(16)) register_26 (
    .D(multiplexer_11_out), .en(and_116_out), .clk(clock_1_out), .Q(register_26_q));  // open: clr
  assign bit_extender_50_out = {{15{and_118_out}}, and_118_out};  // Bit_Extender bit_extender_50
  assign bit_extender_51_out = {{15{and_119_out}}, and_119_out};  // Bit_Extender bit_extender_51
  Register #(.width(16)) register_27 (
    .D(multiplexer_11_out), .en(and_120_out), .clk(clock_1_out), .Q(register_27_q));  // open: clr
  assign bit_extender_52_out = {{15{and_122_out}}, and_122_out};  // Bit_Extender bit_extender_52
  assign bit_extender_53_out = {{15{and_123_out}}, and_123_out};  // Bit_Extender bit_extender_53
  Register #(.width(16)) register_28 (
    .D(multiplexer_11_out), .en(and_124_out), .clk(clock_1_out), .Q(register_28_q));  // open: clr
  assign bit_extender_54_out = {{15{and_126_out}}, and_126_out};  // Bit_Extender bit_extender_54
  assign bit_extender_55_out = {{15{and_127_out}}, and_127_out};  // Bit_Extender bit_extender_55
  Register #(.width(16)) register_29 (
    .D(multiplexer_11_out), .en(and_128_out), .clk(clock_1_out), .Q(register_29_q));  // open: clr
  assign bit_extender_56_out = {{15{and_130_out}}, and_130_out};  // Bit_Extender bit_extender_56
  assign bit_extender_57_out = {{15{and_131_out}}, and_131_out};  // Bit_Extender bit_extender_57
  Register #(.width(16)) register_30 (
    .D(multiplexer_11_out), .en(and_132_out), .clk(clock_1_out), .Q(register_30_q));  // open: clr
  assign bit_extender_58_out = {{15{and_134_out}}, and_134_out};  // Bit_Extender bit_extender_58
  assign bit_extender_59_out = {{15{and_135_out}}, and_135_out};  // Bit_Extender bit_extender_59
  Register #(.width(16)) register_31 (
    .D(multiplexer_11_out), .en(and_136_out), .clk(clock_1_out), .Q(register_31_q));  // open: clr
  assign bit_extender_60_out = {{15{and_138_out}}, and_138_out};  // Bit_Extender bit_extender_60
  assign bit_extender_61_out = {{15{and_139_out}}, and_139_out};  // Bit_Extender bit_extender_61
  assign or_43_out = or_59_out | or_51_out;  // OR_Gate or_43, 16 bits wide
  assign or_44_out = and_140_out | or_45_out;  // OR_Gate or_44, 16 bits wide
  assign and_140_out = register_24_q & bit_extender_46_out;  // AND_Gate and_140, 16 bits wide
  assign and_141_out = register_24_q & bit_extender_47_out;  // AND_Gate and_141, 16 bits wide
  assign or_45_out = and_142_out | or_46_out;  // OR_Gate or_45, 16 bits wide
  assign and_142_out = register_25_q & bit_extender_48_out;  // AND_Gate and_142, 16 bits wide
  assign and_143_out = register_25_q & bit_extender_49_out;  // AND_Gate and_143, 16 bits wide
  assign or_46_out = and_144_out | or_47_out;  // OR_Gate or_46, 16 bits wide
  assign and_144_out = register_26_q & bit_extender_50_out;  // AND_Gate and_144, 16 bits wide
  assign and_145_out = register_26_q & bit_extender_51_out;  // AND_Gate and_145, 16 bits wide
  assign or_47_out = and_146_out | or_48_out;  // OR_Gate or_47, 16 bits wide
  assign and_146_out = register_27_q & bit_extender_52_out;  // AND_Gate and_146, 16 bits wide
  assign and_147_out = register_27_q & bit_extender_53_out;  // AND_Gate and_147, 16 bits wide
  assign or_48_out = and_148_out | or_49_out;  // OR_Gate or_48, 16 bits wide
  assign and_148_out = register_28_q & bit_extender_54_out;  // AND_Gate and_148, 16 bits wide
  assign and_149_out = register_28_q & bit_extender_55_out;  // AND_Gate and_149, 16 bits wide
  assign or_49_out = and_150_out | or_50_out;  // OR_Gate or_49, 16 bits wide
  assign and_150_out = register_29_q & bit_extender_56_out;  // AND_Gate and_150, 16 bits wide
  assign and_151_out = register_29_q & bit_extender_57_out;  // AND_Gate and_151, 16 bits wide
  assign or_50_out = and_152_out | and_154_out;  // OR_Gate or_50, 16 bits wide
  assign and_152_out = register_30_q & bit_extender_58_out;  // AND_Gate and_152, 16 bits wide
  assign and_153_out = register_30_q & bit_extender_59_out;  // AND_Gate and_153, 16 bits wide
  assign and_154_out = register_31_q & bit_extender_60_out;  // AND_Gate and_154, 16 bits wide
  assign and_155_out = register_31_q & bit_extender_61_out;  // AND_Gate and_155, 16 bits wide
  assign or_51_out = and_141_out | or_52_out;  // OR_Gate or_51, 16 bits wide
  assign or_52_out = and_143_out | or_53_out;  // OR_Gate or_52, 16 bits wide
  assign or_53_out = and_145_out | or_54_out;  // OR_Gate or_53, 16 bits wide
  assign or_54_out = and_147_out | or_55_out;  // OR_Gate or_54, 16 bits wide
  assign or_55_out = and_149_out | or_56_out;  // OR_Gate or_55, 16 bits wide
  assign or_56_out = and_151_out | or_57_out;  // OR_Gate or_56, 16 bits wide
  assign or_57_out = and_153_out | and_155_out;  // OR_Gate or_57, 16 bits wide
  and and_156 (and_156_out, ~IMEM_dout[7], ~IMEM_dout[8], ~IMEM_dout[9], IMEM_dout[10], IMEM_dout[11]);  // AND_Gate
  and and_157 (and_157_out, ~IMEM_dout[15], ~IMEM_dout[16], ~IMEM_dout[17], IMEM_dout[18], IMEM_dout[19]);  // AND_Gate
  and and_158 (and_158_out, ~IMEM_dout[20], ~IMEM_dout[21], ~IMEM_dout[22], IMEM_dout[23], IMEM_dout[24]);  // AND_Gate
  and and_159 (and_159_out, IMEM_dout[7], ~IMEM_dout[8], ~IMEM_dout[9], IMEM_dout[10], IMEM_dout[11]);  // AND_Gate
  and and_160 (and_160_out, IMEM_dout[15], ~IMEM_dout[16], ~IMEM_dout[17], IMEM_dout[18], IMEM_dout[19]);  // AND_Gate
  and and_161 (and_161_out, IMEM_dout[20], ~IMEM_dout[21], ~IMEM_dout[22], IMEM_dout[23], IMEM_dout[24]);  // AND_Gate
  and and_162 (and_162_out, ~IMEM_dout[7], IMEM_dout[8], ~IMEM_dout[9], IMEM_dout[10], IMEM_dout[11]);  // AND_Gate
  and and_163 (and_163_out, ~IMEM_dout[15], IMEM_dout[16], ~IMEM_dout[17], IMEM_dout[18], IMEM_dout[19]);  // AND_Gate
  and and_164 (and_164_out, ~IMEM_dout[20], IMEM_dout[21], ~IMEM_dout[22], IMEM_dout[23], IMEM_dout[24]);  // AND_Gate
  and and_165 (and_165_out, IMEM_dout[7], IMEM_dout[8], ~IMEM_dout[9], IMEM_dout[10], IMEM_dout[11]);  // AND_Gate
  and and_166 (and_166_out, IMEM_dout[15], IMEM_dout[16], ~IMEM_dout[17], IMEM_dout[18], IMEM_dout[19]);  // AND_Gate
  and and_167 (and_167_out, IMEM_dout[20], IMEM_dout[21], ~IMEM_dout[22], IMEM_dout[23], IMEM_dout[24]);  // AND_Gate
  and and_168 (and_168_out, ~IMEM_dout[7], ~IMEM_dout[8], IMEM_dout[9], IMEM_dout[10], IMEM_dout[11]);  // AND_Gate
  and and_169 (and_169_out, ~IMEM_dout[15], ~IMEM_dout[16], IMEM_dout[17], IMEM_dout[18], IMEM_dout[19]);  // AND_Gate
  and and_170 (and_170_out, ~IMEM_dout[20], ~IMEM_dout[21], IMEM_dout[22], IMEM_dout[23], IMEM_dout[24]);  // AND_Gate
  and and_171 (and_171_out, IMEM_dout[7], ~IMEM_dout[8], IMEM_dout[9], IMEM_dout[10], IMEM_dout[11]);  // AND_Gate
  and and_172 (and_172_out, IMEM_dout[15], ~IMEM_dout[16], IMEM_dout[17], IMEM_dout[18], IMEM_dout[19]);  // AND_Gate
  and and_173 (and_173_out, IMEM_dout[20], ~IMEM_dout[21], IMEM_dout[22], IMEM_dout[23], IMEM_dout[24]);  // AND_Gate
  and and_174 (and_174_out, ~IMEM_dout[7], IMEM_dout[8], IMEM_dout[9], IMEM_dout[10], IMEM_dout[11]);  // AND_Gate
  and and_175 (and_175_out, ~IMEM_dout[15], IMEM_dout[16], IMEM_dout[17], IMEM_dout[18], IMEM_dout[19]);  // AND_Gate
  and and_176 (and_176_out, ~IMEM_dout[20], IMEM_dout[21], IMEM_dout[22], IMEM_dout[23], IMEM_dout[24]);  // AND_Gate
  and and_177 (and_177_out, IMEM_dout[7], IMEM_dout[8], IMEM_dout[9], IMEM_dout[10], IMEM_dout[11]);
  and and_178 (and_178_out, IMEM_dout[15], IMEM_dout[16], IMEM_dout[17], IMEM_dout[18], IMEM_dout[19]);
  and and_179 (and_179_out, IMEM_dout[20], IMEM_dout[21], IMEM_dout[22], IMEM_dout[23], IMEM_dout[24]);
  Register #(.width(16)) register_32 (
    .D(multiplexer_11_out), .en(and_180_out), .clk(clock_1_out), .Q(register_32_q));  // open: clr
  and and_180 (and_180_out, nor_1_out, and_156_out);
  Register #(.width(16)) register_33 (
    .D(multiplexer_11_out), .en(and_181_out), .clk(clock_1_out), .Q(register_33_q));  // open: clr
  and and_181 (and_181_out, nor_1_out, and_159_out);
  Register #(.width(16)) register_34 (
    .D(multiplexer_11_out), .en(and_182_out), .clk(clock_1_out), .Q(register_34_q));  // open: clr
  and and_182 (and_182_out, nor_1_out, and_162_out);
  Register #(.width(16)) register_35 (
    .D(multiplexer_11_out), .en(and_183_out), .clk(clock_1_out), .Q(register_35_q));  // open: clr
  and and_183 (and_183_out, nor_1_out, and_165_out);
  Register #(.width(16)) register_36 (
    .D(multiplexer_11_out), .en(and_184_out), .clk(clock_1_out), .Q(register_36_q));  // open: clr
  and and_184 (and_184_out, nor_1_out, and_168_out);
  Register #(.width(16)) register_37 (
    .D(multiplexer_11_out), .en(and_185_out), .clk(clock_1_out), .Q(register_37_q));  // open: clr
  and and_185 (and_185_out, nor_1_out, and_171_out);
  Register #(.width(16)) register_38 (
    .D(multiplexer_11_out), .en(and_186_out), .clk(clock_1_out), .Q(register_38_q));  // open: clr
  and and_186 (and_186_out, nor_1_out, and_174_out);
  Register #(.width(16)) register_39 (
    .D(multiplexer_11_out), .en(and_187_out), .clk(clock_1_out), .Q(register_39_q));  // open: clr
  and and_187 (and_187_out, nor_1_out, and_177_out);
  assign bit_extender_62_out = {{15{and_157_out}}, and_157_out};  // Bit_Extender bit_extender_62
  assign bit_extender_63_out = {{15{and_158_out}}, and_158_out};  // Bit_Extender bit_extender_63
  assign bit_extender_64_out = {{15{and_160_out}}, and_160_out};  // Bit_Extender bit_extender_64
  assign bit_extender_65_out = {{15{and_161_out}}, and_161_out};  // Bit_Extender bit_extender_65
  assign bit_extender_66_out = {{15{and_163_out}}, and_163_out};  // Bit_Extender bit_extender_66
  assign bit_extender_67_out = {{15{and_164_out}}, and_164_out};  // Bit_Extender bit_extender_67
  assign bit_extender_68_out = {{15{and_166_out}}, and_166_out};  // Bit_Extender bit_extender_68
  assign bit_extender_69_out = {{15{and_167_out}}, and_167_out};  // Bit_Extender bit_extender_69
  assign bit_extender_70_out = {{15{and_169_out}}, and_169_out};  // Bit_Extender bit_extender_70
  assign bit_extender_71_out = {{15{and_170_out}}, and_170_out};  // Bit_Extender bit_extender_71
  assign bit_extender_72_out = {{15{and_172_out}}, and_172_out};  // Bit_Extender bit_extender_72
  assign bit_extender_73_out = {{15{and_173_out}}, and_173_out};  // Bit_Extender bit_extender_73
  assign bit_extender_74_out = {{15{and_175_out}}, and_175_out};  // Bit_Extender bit_extender_74
  assign bit_extender_75_out = {{15{and_176_out}}, and_176_out};  // Bit_Extender bit_extender_75
  assign bit_extender_76_out = {{15{and_178_out}}, and_178_out};  // Bit_Extender bit_extender_76
  assign bit_extender_77_out = {{15{and_179_out}}, and_179_out};  // Bit_Extender bit_extender_77
  assign or_58_out = and_188_out | or_60_out;  // OR_Gate or_58, 16 bits wide
  assign or_59_out = and_189_out | or_61_out;  // OR_Gate or_59, 16 bits wide
  assign and_188_out = register_32_q & bit_extender_62_out;  // AND_Gate and_188, 16 bits wide
  assign and_189_out = register_32_q & bit_extender_63_out;  // AND_Gate and_189, 16 bits wide
  assign or_60_out = and_190_out | or_62_out;  // OR_Gate or_60, 16 bits wide
  assign or_61_out = and_191_out | or_63_out;  // OR_Gate or_61, 16 bits wide
  assign and_190_out = register_33_q & bit_extender_64_out;  // AND_Gate and_190, 16 bits wide
  assign and_191_out = register_33_q & bit_extender_65_out;  // AND_Gate and_191, 16 bits wide
  assign or_62_out = and_192_out | or_64_out;  // OR_Gate or_62, 16 bits wide
  assign or_63_out = and_193_out | or_65_out;  // OR_Gate or_63, 16 bits wide
  assign and_192_out = register_34_q & bit_extender_66_out;  // AND_Gate and_192, 16 bits wide
  assign and_193_out = register_34_q & bit_extender_67_out;  // AND_Gate and_193, 16 bits wide
  assign or_64_out = and_194_out | or_66_out;  // OR_Gate or_64, 16 bits wide
  assign or_65_out = and_195_out | or_67_out;  // OR_Gate or_65, 16 bits wide
  assign and_194_out = register_35_q & bit_extender_68_out;  // AND_Gate and_194, 16 bits wide
  assign and_195_out = register_35_q & bit_extender_69_out;  // AND_Gate and_195, 16 bits wide
  assign or_66_out = and_196_out | or_68_out;  // OR_Gate or_66, 16 bits wide
  assign or_67_out = and_197_out | or_69_out;  // OR_Gate or_67, 16 bits wide
  assign and_196_out = register_36_q & bit_extender_70_out;  // AND_Gate and_196, 16 bits wide
  assign and_197_out = register_36_q & bit_extender_71_out;  // AND_Gate and_197, 16 bits wide
  assign or_68_out = and_198_out | or_70_out;  // OR_Gate or_68, 16 bits wide
  assign or_69_out = and_199_out | or_71_out;  // OR_Gate or_69, 16 bits wide
  assign and_198_out = register_37_q & bit_extender_72_out;  // AND_Gate and_198, 16 bits wide
  assign and_199_out = register_37_q & bit_extender_73_out;  // AND_Gate and_199, 16 bits wide
  assign or_70_out = and_200_out | and_202_out;  // OR_Gate or_70, 16 bits wide
  assign or_71_out = and_201_out | and_203_out;  // OR_Gate or_71, 16 bits wide
  assign and_200_out = register_38_q & bit_extender_74_out;  // AND_Gate and_200, 16 bits wide
  assign and_201_out = register_38_q & bit_extender_75_out;  // AND_Gate and_201, 16 bits wide
  assign and_202_out = register_39_q & bit_extender_76_out;  // AND_Gate and_202, 16 bits wide
  assign and_203_out = register_39_q & bit_extender_77_out;  // AND_Gate and_203, 16 bits wide
  DotMatrix #(.inputtype("row"), .matrixcols(16), .matrixrows(16)) dotmatrix_1 (
    .row0(register_1_q_2), .row1(register_1_q), .row2(register_3_q_2), .row3(register_3_q),
    .row4(register_5_q_2), .row5(register_5_q), .row6(register_7_q[31:16]), .row7(register_7_q[15:0]),
    .row8(register_2_q_2), .row9(register_2_q), .row10(register_4_q_2), .row11(register_4_q),
    .row12(register_6_q[31:16]), .row13(register_6_q[15:0]), .row14(register_8_q[31:16]),
    .row15(register_8_q[15:0]));
  // Pins of 16 and 32 bits meet at or_10_out
  // Pins of 16 and 32 bits meet at PC_q
  // Pins of 4 and 16 bits meet at multiplexer_5_out
  // Pins of 16 and 17 bits meet at shifter_2_out
  // Pins of 16 and 17 bits meet at multiplexer_7_out
  // Pins of 4 and 16 bits meet at multiplexer_5_out
  // Pins of 16 and 17 bits meet at shifter_3_out
  // Pins of 4 and 16 bits meet at multiplexer_5_out
  // Pins of 16 and 32 bits meet at or_11_out
  // Pins of 16 and 32 bits meet at or_2_out
  // Pins of 16 and 32 bits meet at multiplexer_10_out
  // Pins of 16 and 32 bits meet at adder_1_out

  // Notes on the sheet:
  //   Branch Comp
  //   I/O
  //   Imm Gen
  //   Control Logic
  //   load
  //   ALU_imm
  //   auipc
  //   store
  //   ALU_reg
  //   lui
  //   branch
  //   jalr
  //   jal
  //   ALU
  //   rsA
  //   rsB
  //   Reg File
endmodule
